# Fritzing sketch arduino-altimeter (saved by Fritzing 0.9.5d)

parts:
  Composant1 = Arduino Nano (Rev3.0)
  M1 = BME280

nets:
  GND: Composant1.GND, M1.GND
  N1: Composant1.A5, M1.SCL
  N2: Composant1.A4, M1.SDA
  3V3: Composant1.3V3, M1.VIN

custom parts:
  BME280: Temperature Humidity Barometric presure Sensor
